// Logisim project 3bit-klokke-feil.circ as structural Verilog: 1 circuit, main circuit main
module main (
  input  x2,
  input  x1,
  input  x0
);

  wire A_2_out, A_3_out, A_4_out, A_out, B_2_out, B_3_out, B_out, C_out, D_2_out, D_3_out, D_4_out, d_5_out,
       D_out, E_2_out, E_3_out, E_out, F_2_out, F_3_out, F_4_out, F_out, G_2_out, G_3_out, G_4_out, G_out,
       not_1_out, not_2_out, not_3_out;

  not not_1 (not_1_out, x2);
  not not_2 (not_2_out, x1);
  not not_3 (not_3_out, x0);
  and A (A_out, x0, not_1_out);
  and A_2 (A_2_out, x1, not_1_out);
  and A_3 (A_3_out, not_1_out, not_3_out);
  and B (B_out, x1, x0);
  and B_2 (B_2_out, x1, not_3_out);
  and D (D_out, not_1_out, not_3_out);
  and D_2 (D_2_out, x1, not_1_out);
  and D_3 (D_3_out, x1, not_3_out);
  and D_4 (D_4_out, x2, not_2_out, not_3_out);
  and E (E_out, not_3_out, not_1_out);
  and E_2 (E_2_out, x1, not_3_out);
  and F (F_out, x2, not_2_out);
  and F_2 (F_2_out, x2, not_3_out);
  and F_3 (F_3_out, not_2_out, not_3_out);
  and G (G_out, x2, not_3_out);
  and G_2 (G_2_out, not_2_out, x2);
  and G_3 (G_3_out, x1, not_1_out);
  or A_4 (A_4_out, A_out, A_2_out, A_3_out);
  or B_3 (B_3_out, not_1_out, B_out, B_2_out);
  or C (C_out, x2, not_2_out, not_3_out);
  or d_5 (d_5_out, D_out, D_2_out, D_3_out, D_4_out);
  or E_3 (E_3_out, E_out, E_2_out);
  or F_4 (F_4_out, F_out, F_2_out, F_3_out);
  or G_4 (G_4_out, G_out, G_2_out, G_3_out);
  _7_Segment_Display u_7_segment_display_1 (
    .g(G_4_out), .f(F_4_out), .a(A_4_out), .b(B_3_out), .e(E_3_out), .d(d_5_out), .c(C_out));  // open: dp
endmodule
