// Logisim project 3bit-klokke.circ as structural Verilog: 1 circuit, main circuit main
module main (
  input  x2,
  input  x1,
  input  x0
);

  wire A_out, and_1_out, and_2_out, and_3_out, and_4_out, and_5_out, and_6_out, and_7_out, and_8_out,
       and_9_out, and_10_out, and_11_out, and_12_out, and_13_out, and_14_out, and_15_out, and_16_out,
       and_17_out, B_out, C_out, D_out, E_out, F_out, G_out, not_1_out, not_2_out, not_3_out;

  and and_1 (and_1_out, not_3_out, not_1_out);
  and and_2 (and_2_out, x1, not_1_out);
  and and_3 (and_3_out, x0, x2);
  and and_4 (and_4_out, x0, x1);
  and and_5 (and_5_out, not_3_out, not_2_out);
  and and_6 (and_6_out, not_1_out, not_3_out);
  and and_7 (and_7_out, x1, not_1_out);
  and and_8 (and_8_out, x1, not_3_out);
  and and_9 (and_9_out, x2, not_2_out, x0);
  and and_10 (and_10_out, not_1_out, not_3_out);
  and and_11 (and_11_out, x1, not_3_out);
  or A (A_out, and_1_out, and_2_out, and_3_out);
  or B (B_out, not_1_out, and_4_out, and_5_out);
  or C (C_out, x2, not_2_out, x0);
  or D (D_out, and_6_out, and_7_out, and_8_out, and_9_out);
  or E (E_out, and_10_out, and_11_out);
  not not_1 (not_1_out, x2);
  not not_2 (not_2_out, x1);
  _7_Segment_Display u_7_segment_display_1 (
    .g(G_out), .f(F_out), .a(A_out), .b(B_out), .e(E_out), .d(D_out), .c(C_out));  // open: dp
  or F (F_out, and_12_out, and_13_out, and_14_out);
  or G (G_out, and_15_out, and_16_out, and_17_out);
  not not_3 (not_3_out, x0);
  and and_12 (and_12_out, x2, not_2_out);
  and and_13 (and_13_out, x2, not_3_out);
  and and_14 (and_14_out, not_2_out, not_3_out);
  and and_15 (and_15_out, x2, not_3_out);
  and and_16 (and_16_out, x2, not_2_out);
  and and_17 (and_17_out, not_1_out, x1);
endmodule
