// Logisim project oblig2-erikoga.circ as structural Verilog: 2 circuits, main circuit main
module main (
);

  wire _0_q, _1_2_q, _1_out, _2_out, _3_out, _4_out, _5_out, _6_out, _7_out, Clk_out, kodelogikk_1_d0,
       kodelogikk_1_d1, kodelogikk_1_out;
  wire [2:0] priority_encoder_1_out;

  Button _1 (.out(_1_out));
  Button _4 (.out(_4_out));
  Button _7 (.out(_7_out));
  Button _2 (.out(_2_out));
  Button _3 (.out(_3_out));
  Button _6 (.out(_6_out));
  Button _5 (.out(_5_out));
  Priority_Encoder priority_encoder_1 (
    .in1(_1_out), .in2(_2_out), .in3(_3_out), .in4(_4_out), .in5(_5_out), .in6(_6_out), .in7(_7_out),
    .out(priority_encoder_1_out));  // open: in0, en_in, gs, en_out
  Clock Clk (.out(Clk_out));
  kodelogikk kodelogikk_1 (
    .q1(_1_2_q), .q0(_0_q), .x2(priority_encoder_1_out[2]), .x1(priority_encoder_1_out[1]),
    .x0(priority_encoder_1_out[0]), .out(kodelogikk_1_out), .d1(kodelogikk_1_d1), .d0(kodelogikk_1_d0));
  D_Flip_Flop _1_2 (.clk(Clk_out), .D(kodelogikk_1_out), .Q(_1_2_q));  // open: Qn, preset, en, reset
  D_Flip_Flop _0 (.clk(Clk_out), .D(kodelogikk_1_d1), .Q(_0_q));  // open: Qn, preset, en, reset
  LED Open (.in(kodelogikk_1_d0));

  // Notes on the sheet:
  //   Koden er 2 4 6
endmodule

// kode
module kodelogikk (
  input  q1,
  input  q0,
  input  x2,
  input  x1,
  input  x0,
  output out,
  output d1,
  output d0
);

  wire nand_1_out, nand_2_out, nand_3_out, nand_4_out, nand_5_out, nand_6_out, nand_7_out, nand_8_out,
       nand_9_out, nand_10_out, nand_11_out, nand_12_out, nand_13_out, nand_14_out, nand_15_out, nand_16_out,
       nand_17_out, nand_18_out, nand_19_out, nand_20_out, nand_21_out, nand_22_out, nand_23_out;

  nand nand_1 (nand_1_out, q1, q1);
  nand nand_2 (nand_2_out, x1, x1);
  nand nand_3 (nand_3_out, x0, x0);
  nand nand_4 (nand_4_out, q0, q0);
  nand nand_5 (nand_5_out, x1, x1);
  nand nand_6 (nand_6_out, x0, x0);
  nand nand_7 (nand_7_out, q0, q0);
  nand nand_8 (nand_8_out, x0, x0);
  nand nand_9 (nand_9_out, q1, q1);
  nand nand_10 (nand_10_out, x2, x2);
  nand nand_11 (nand_11_out, x0, x0);
  nand nand_12 (nand_12_out, q1, q1);
  nand nand_13 (nand_13_out, x2, x2);
  nand nand_14 (nand_14_out, x0, x0);
  nand nand_15 (nand_15_out, q0, q0);
  nand nand_16 (nand_16_out, x0, x0);
  nand nand_17 (nand_17_out, q1, q0);
  nand nand_18 (nand_18_out, nand_1_out, q0, x2, nand_2_out, nand_3_out);
  nand nand_19 (nand_19_out, q1, nand_4_out, nand_5_out, nand_6_out);
  nand nand_20 (nand_20_out, q1, nand_7_out, x2, nand_8_out);
  nand nand_21 (nand_21_out, nand_9_out, nand_10_out, x1, nand_11_out);
  nand nand_22 (nand_22_out, nand_12_out, q0, nand_13_out, nand_14_out);
  nand nand_23 (nand_23_out, q1, nand_15_out, x2, x1, nand_16_out);
  nand nand_24 (d0, nand_17_out, nand_17_out);
  nand nand_25 (out, nand_18_out, nand_19_out, nand_20_out);
  nand nand_26 (d1, nand_21_out, nand_22_out, nand_23_out);

  // Notes on the sheet:
  //   Kodelås logikk - koden er 2 - 4 - 6
endmodule
